// Logisim project index.circ as structural Verilog
module _6x64_Decoder (
  input  S0,
  input  S1,
  input  S2,
  input  S3,
  input  S4,
  input  S5,
  input  Enable,
  output Out_0,
  output Out_1,
  output Out_2,
  output Out_3,
  output Out_4,
  output Out_5,
  output Out_6,
  output Out_7,
  output Out_8,
  output Out_9,
  output Out_10,
  output Out_11,
  output Out_12,
  output Out_13,
  output Out_14,
  output Out_15,
  output Out_16,
  output Out_17,
  output Out_18,
  output Out_19,
  output Out_20,
  output Out_21,
  output Out_22,
  output Out_23,
  output Out_24,
  output Out_25,
  output Out_26,
  output Out_27,
  output Out_28,
  output Out_29,
  output Out_30,
  output Out_31,
  output Out_32,
  output Out_33,
  output Out_34,
  output Out_35,
  output Out_36,
  output Out_37,
  output Out_38,
  output Out_39,
  output Out_40,
  output Out_41,
  output Out_42,
  output Out_43,
  output Out_44,
  output Out_45,
  output Out_46,
  output Out_47,
  output Out_48,
  output Out_49,
  output Out_50,
  output Out_51,
  output Out_52,
  output Out_53,
  output Out_54,
  output Out_55,
  output Out_56,
  output Out_57,
  output Out_58,
  output Out_59,
  output Out_60,
  output Out_61,
  output Out_62,
  output Out_63
);

  wire and_1_out, and_2_out, and_3_out, and_4_out, decoder_1_out0, decoder_1_out1, decoder_1_out2,
       decoder_1_out3;

  Decoder #(.select(2)) decoder_1 (
    .out0(decoder_1_out0), .out1(decoder_1_out1), .out2(decoder_1_out2), .out3(decoder_1_out3),
    .sel({S5, S4}), .en(Enable));
  and and_1 (and_1_out, decoder_1_out0, Enable);
  and and_2 (and_2_out, decoder_1_out1, Enable);
  and and_3 (and_3_out, Enable, decoder_1_out2);
  and and_4 (and_4_out, decoder_1_out3, Enable);
  Decoder #(.select(4), .disabled(0)) decoder_2 (
    .out0(Out_0), .out1(Out_1), .out2(Out_2), .out3(Out_3), .out4(Out_4), .out5(Out_5), .out6(Out_6),
    .out7(Out_7), .out8(Out_8), .out9(Out_9), .out10(Out_10), .out11(Out_11), .out12(Out_12), .out13(Out_13),
    .out14(Out_14), .out15(Out_15), .sel({S3, S2, S1, S0}), .en(and_1_out));
  Decoder #(.select(4), .disabled(0)) decoder_3 (
    .out0(Out_16), .out1(Out_17), .out2(Out_18), .out3(Out_19), .out4(Out_20), .out5(Out_21), .out6(Out_22),
    .out7(Out_23), .out8(Out_24), .out9(Out_25), .out10(Out_26), .out11(Out_27), .out12(Out_28),
    .out13(Out_29), .out14(Out_30), .out15(Out_31), .sel({S3, S2, S1, S0}), .en(and_2_out));
  Decoder #(.select(4), .disabled(0)) decoder_4 (
    .out0(Out_32), .out1(Out_33), .out2(Out_34), .out3(Out_35), .out4(Out_36), .out5(Out_37), .out6(Out_38),
    .out7(Out_39), .out8(Out_40), .out9(Out_41), .out10(Out_42), .out11(Out_43), .out12(Out_44),
    .out13(Out_45), .out14(Out_46), .out15(Out_47), .sel({S3, S2, S1, S0}), .en(and_3_out));
  Decoder #(.select(4), .disabled(0)) decoder_5 (
    .out0(Out_48), .out1(Out_49), .out2(Out_50), .out3(Out_51), .out4(Out_52), .out5(Out_53), .out6(Out_54),
    .out7(Out_55), .out8(Out_56), .out9(Out_57), .out10(Out_58), .out11(Out_59), .out12(Out_60),
    .out13(Out_61), .out14(Out_62), .out15(Out_63), .sel({S3, S2, S1, S0}), .en(and_4_out));
endmodule
